# Fritzing sketch encoders (saved by Fritzing 0.9.10b)
breadboards: 1

parts:
  RE1 = Rotary Encoder [package=THT]
  RE2 = Rotary Encoder [package=THT]  # not connected
  R1 = Resistor [tolerance=±5% resistance=10k package="2010 [SMD]"]  # not connected
  R2 = Resistor [tolerance=±5% resistance=10k package="2010 [SMD]"]  # not connected
  R3 = Resistor [tolerance=±5% resistance=10k package="2010 [SMD]"]  # not connected
  U2 = OP37 - Low Noise, Precision, High Speed Op Amp [part_number=OP37]
  SP1 = SPEAKER [package=pcb_mount_speaker]  # not connected
  R4 = Slide Potentiometer [maximum_resistance=100kΩ knob_status=50% power=0.5W]  # not connected
  R5 = Slide Potentiometer [maximum_resistance=100kΩ knob_status=50% power=0.5W]

nets:
  N1: RE1.EncoderPinB, R5.leg1
  N2: U2.-IN, U2.V+
  N3: U2.+IN, U2.OUT
  N4: U2.-V, U2.NC
